// Digital circuit frontpanel.dig as structural Verilog
module frontpanel (
  input  clock,
  output [15:0] R0,
  output [15:0] R1,
  output [15:0] R2,
  output [15:0] R3,
  output [3:0] PC,
  output halt,
  output error
);

  wire advance_out, control_1_p4, fetch_1_p6, hex, hexdisplay_1_p2, hexdisplay_1_p5, hexdisplay_1_p8,
       hexdisplay_1_p10, hexdisplay_1_p13, hexdisplay_2_p2, hexdisplay_2_p5, hexdisplay_2_p8,
       hexdisplay_2_p10, hexdisplay_2_p13, instrdisplay_1_p2, instrdisplay_1_p4, instrdisplay_1_p7,
       instrdisplay_1_p9, instrdisplay_1_p12, instrdisplay_1_p14, jump, op, or_1_out, pmshim_1_c, pmshim_1_l,
       pmshim_1_s, rd_valid, regdisplay_1_p3, regdisplay_1_p7, regdisplay_2_p3, regdisplay_2_p7, rs_valid,
       sys, T;
  wire [2:0] control_1_p5;
  wire [3:0] hexdisplay_1_p1, hexdisplay_1_p4, hexdisplay_1_p6, hexdisplay_1_p9, hexdisplay_1_p12,
       hexdisplay_2_p1, hexdisplay_2_p4, hexdisplay_2_p6, hexdisplay_2_p9, hexdisplay_2_p12, pmshim_1_a, rd,
       rs;
  wire [15:0] decoder_1_p1, decoder_1_p2, execute_1_result, instrdisplay_1_p1, instrdisplay_1_p3,
       instrdisplay_1_p6, instrdisplay_1_p8, instrdisplay_1_p10, instrdisplay_1_p13, L, pmshim_1_d,
       Program_d, R, regdisplay_1_p1, regdisplay_1_p5, regdisplay_2_p1, regdisplay_2_p5;

  pmshim pmshim_1 (.pc(PC), .A(pmshim_1_a), .D(pmshim_1_d), .s(pmshim_1_s), .C(pmshim_1_c), .L(pmshim_1_l));
  Button advance (.out(advance_out));
  EEPROMDualPort #(.AddrBits(4), .isProgramMemory("true"), .Bits(16)) Program (
    .A(pmshim_1_a), .Din(pmshim_1_d), .str(pmshim_1_s), .C(pmshim_1_c), .ld(pmshim_1_l), .D(Program_d));
  or or_1 (or_1_out, advance_out, clock);
  SixteenSeg sixteenseg_1 (.led(regdisplay_1_p1), .dp(regdisplay_1_p3));
  // regdisplay regdisplay_1: pin names not known; wires that end beside it: regdisplay_1_p1, 1'b1, regdisplay_1_p3, jump, regdisplay_1_p5, rd, regdisplay_1_p7
  SixteenSeg sixteenseg_2 (.led(regdisplay_1_p5), .dp(regdisplay_1_p7));
  // fetch fetch_1: pin names not known; wires that end beside it: Program_d, or_1_out, R, jump, PC, fetch_1_p6
  Seven_Seg_Hex seven_seg_hex_1 (.d(hexdisplay_1_p1), .dp(hexdisplay_1_p2));
  Seven_Seg_Hex seven_seg_hex_2 (.d(hexdisplay_1_p4), .dp(hexdisplay_1_p5));
  // hexdisplay hexdisplay_1: pin names not known; wires that end beside it: hexdisplay_1_p1, hexdisplay_1_p2, rd_valid, hexdisplay_1_p4, hexdisplay_1_p5, hexdisplay_1_p6, L, hexdisplay_1_p8, hexdisplay_1_p9, hexdisplay_1_p10, hex, hexdisplay_1_p12, hexdisplay_1_p13
  Seven_Seg_Hex seven_seg_hex_3 (.d(hexdisplay_1_p6), .dp(hexdisplay_1_p8));
  Seven_Seg_Hex seven_seg_hex_4 (.d(hexdisplay_1_p9), .dp(hexdisplay_1_p10));
  // decoder decoder_1: pin names not known; wires that end beside it: decoder_1_p1, decoder_1_p2, fetch_1_p6, rs, rd, L, R, sys, op, rs_valid, rd_valid
  Seven_Seg_Hex seven_seg_hex_5 (.d(hexdisplay_1_p12), .dp(hexdisplay_1_p13));
  SixteenSeg sixteenseg_3 (.led(instrdisplay_1_p1), .dp(instrdisplay_1_p2));
  // instrdisplay instrdisplay_1: pin names not known; wires that end beside it: instrdisplay_1_p1, instrdisplay_1_p2, instrdisplay_1_p3, instrdisplay_1_p4, sys, instrdisplay_1_p6, instrdisplay_1_p7, instrdisplay_1_p8, instrdisplay_1_p9, instrdisplay_1_p10, op, instrdisplay_1_p12, instrdisplay_1_p13, instrdisplay_1_p14
  SixteenSeg sixteenseg_4 (.led(instrdisplay_1_p3), .dp(instrdisplay_1_p4));
  SixteenSeg sixteenseg_5 (.led(instrdisplay_1_p6), .dp(instrdisplay_1_p7));
  SixteenSeg sixteenseg_6 (.led(instrdisplay_1_p8), .dp(instrdisplay_1_p9));
  SixteenSeg sixteenseg_7 (.led(instrdisplay_1_p10), .dp(instrdisplay_1_p12));
  // control control_1: pin names not known; wires that end beside it: sys, op, or_1_out, control_1_p4, control_1_p5, T, halt, error, jump
  SixteenSeg sixteenseg_8 (.led(instrdisplay_1_p13), .dp(instrdisplay_1_p14));
  Seven_Seg_Hex seven_seg_hex_6 (.d(hexdisplay_2_p1), .dp(hexdisplay_2_p2));
  Seven_Seg_Hex seven_seg_hex_7 (.d(hexdisplay_2_p4), .dp(hexdisplay_2_p5));
  // hexdisplay hexdisplay_2: pin names not known; wires that end beside it: hexdisplay_2_p1, hexdisplay_2_p2, 1'b1, hexdisplay_2_p4, hexdisplay_2_p5, hexdisplay_2_p6, R, hexdisplay_2_p8, hexdisplay_2_p9, hexdisplay_2_p10, hex, hexdisplay_2_p12, hexdisplay_2_p13
  execute execute_1 (.L(L), .R(R), .cond(control_1_p5), .result(execute_1_result), .skip_n(control_1_p4));  // open: op
  Seven_Seg_Hex seven_seg_hex_8 (.d(hexdisplay_2_p6), .dp(hexdisplay_2_p8));
  Seven_Seg_Hex seven_seg_hex_9 (.d(hexdisplay_2_p9), .dp(hexdisplay_2_p10));
  DipSwitch u_hex (.out(hex));
  Seven_Seg_Hex seven_seg_hex_10 (.d(hexdisplay_2_p12), .dp(hexdisplay_2_p13));
  SixteenSeg sixteenseg_9 (.led(regdisplay_2_p1), .dp(regdisplay_2_p3));
  // regdisplay regdisplay_2: pin names not known; wires that end beside it: regdisplay_2_p1, rs_valid, regdisplay_2_p3, 1'b0, regdisplay_2_p5, rs, regdisplay_2_p7
  regfile regfile_1 (
    .rs(rs), .rd(rd), .result(execute_1_result), .clock(or_1_out), .rdval(decoder_1_p1),
    .rsval(decoder_1_p2), .R0(R0), .R1(R1), .R2(R2), .R3(R3));  // open: en
  SixteenSeg sixteenseg_10 (.led(regdisplay_2_p5), .dp(regdisplay_2_p7));
  LED u_T (.in(T));

  // Notes on the sheet:
  //   contents of Program (hex, n*v repeats v):
  //   c1,8082,8102,101,1313,21,1b0b,81,2a03,1
  //   rj45 Creates
endmodule
